# Fritzing sketch rpi (saved by Fritzing 0.9.2b)
perfboards: 1

parts:
  J1 = shrouded pin header, 26 pins [form="♂ (shrouded male)"]
  Part1 = SparkFun T5403 Barometer Breakout
  Raspberry_Pi_B_rev1 = Raspberry Pi B rev1  # not connected

nets:
  N1: J1.pin2, Part1.SDA/MOSI
  N2: J1.pin3, Part1.SCL/SCLK
  N3: J1.pin9, Part1.VCC
  N4: J1.pin13, Part1.GND

custom parts:
  SparkFun T5403 Barometer Breakout: A breakout for the SparkFun T5403 Barometer.
