# Fritzing sketch verkstad.ver.1 (saved by Fritzing 0.9.2b)
perfboards: 1

parts:
  Part1 = Arduino Pro Mini v13
  Part2 = XBee Explorer Regulated  # not connected
  RHT1 = Humidity and Temperature Sensor RHT03
  S1 = Momentary Switch [package=ksa_sealed_tac_switch]
  R1 = TRIMPOT [package=3362u-2]
  U1 = LCD-16X2 [package=lcd-16x2_noholes]  # not connected
  JP1 = M16 [package=1x16_machine-pin-header_lock.004]
  R2 = Resistor [tolerance=±5% resistance=220 package="0603 [SMD]"]
  R3 = Resistor [tolerance=±5% resistance=220 package="0603 [SMD]"]

nets:
  N1: Part1.GND, RHT1.GND_2, R1.CW, JP1.1, JP1.16
  VCC: Part1.VCC, RHT1.Vcc, S1.1, R1.CCW, R2.Pin_1, R3.Pin_0
  N2: Part1.D9_PWM, S1.3
  N3: Part1.D8, JP1.3
  N4: Part1.D7, JP1.4
  N5: Part1.D6_PWM, JP1.5
  N6: Part1.D5_PWM, JP1.6
  N7: Part1.D4, JP1.11
  N8: Part1.D3_PWM, JP1.13
  N9: Part1.D2, RHT1.Data-signal, R3.Pin_1
  N10: R1.WIPER, JP1.14
  N11: JP1.2, R2.Pin_0
